// Logisim project Lockbox.circ as structural Verilog
module main (
);

  wire oled_screen_1_approved, oled_screen_1_not_approved, raspberry_pi_pico_1_gnd,
       raspberry_pi_pico_1_gpio20_sda, raspberry_pi_pico_1_gpio21_scl, raspberry_pi_pico_1_gpio_16_tx,
       raspberry_pi_pico_1_gpio_18_pwm, raspberry_pi_pico_1_v_out_3_3v, raspberry_pi_pico_1_v_out_5v,
       Servo_Connected_To_3D_Printed_Lock_lock_rotating, uart_fingerprint_sensor_1_tx;

  OLED_Screen oled_screen_1 (
    .VIN_5V(raspberry_pi_pico_1_v_out_5v), .GND(raspberry_pi_pico_1_gnd),
    .SDA(raspberry_pi_pico_1_gpio20_sda), .SCL(raspberry_pi_pico_1_gpio21_scl),
    .Approved(oled_screen_1_approved), .Not_Approved(oled_screen_1_not_approved));
  Raspberry_Pi_Pico raspberry_pi_pico_1 (
    .Micro_USB_Power(1'b1), .GPIO_17_RX(uart_fingerprint_sensor_1_tx),
    .V_Out_3_3V(raspberry_pi_pico_1_v_out_3_3v), .GND(raspberry_pi_pico_1_gnd),
    .GPIO_16_TX(raspberry_pi_pico_1_gpio_16_tx), .V_Out_5V(raspberry_pi_pico_1_v_out_5v),
    .GPIO_18_PWM(raspberry_pi_pico_1_gpio_18_pwm), .GPIO20_SDA(raspberry_pi_pico_1_gpio20_sda),
    .GPIO21_SCL(raspberry_pi_pico_1_gpio21_scl));
  UART_Fingerprint_Sensor uart_fingerprint_sensor_1 (
    .VIN_3_3V(raspberry_pi_pico_1_v_out_3_3v), .GND(raspberry_pi_pico_1_gnd),
    .RX(raspberry_pi_pico_1_gpio_16_tx), .EN(1'b1), .TX(uart_fingerprint_sensor_1_tx));
  Servo Servo_Connected_To_3D_Printed_Lock (
    .PWM_Data(raspberry_pi_pico_1_gpio_18_pwm), .VIN_5V(raspberry_pi_pico_1_v_out_5v),
    .GND(raspberry_pi_pico_1_gnd), .Lock_Rotating(Servo_Connected_To_3D_Printed_Lock_lock_rotating));
  Lockbox Physical_Lockbox_Lid ();

  // Notes on the sheet:
  //   Power via Micro_USB
  //   Screen Shows "Approved"
  //   Screen Shows "Not Approved, Try Again"
  //   EN always High due to constant plugging in and out of USB power
endmodule

module Raspberry_Pi_Pico (
  input  Micro_USB_Power,
  input  GPIO_17_RX,
  output V_Out_3_3V,
  output GND,
  output GPIO_16_TX,
  output V_Out_5V,
  output GPIO_18_PWM,
  output GPIO20_SDA,
  output GPIO21_SCL
);
endmodule

module UART_Fingerprint_Sensor (
  input  VIN_3_3V,
  input  GND,
  input  RX,
  input  EN,
  output TX
);
endmodule

module Servo (
  input  PWM_Data,
  input  VIN_5V,
  input  GND,
  output Lock_Rotating
);
endmodule

module OLED_Screen (
  input  VIN_5V,
  input  GND,
  input  SDA,
  input  SCL,
  output Approved,
  output Not_Approved
);
endmodule
